// Digital circuit Circuito_SIMD.dig as structural Verilog
module Circuito_SIMD (
  input  CLOCK,
  input  RESET,
  input  LOAD_ENABLE,
  input  [4:0] REG_SEL,
  output [31:0] PC,
  output [31:0] INSTR,
  output [31:0] ALU_RESULT,
  output [31:0] REG_DEBUG,
  output HAZARD_STALL,
  output HAZARD_FLUSH,
  output [31:0] VEC_LANE0,
  output [31:0] VEC_LANE1,
  output [31:0] VEC_LANE2,
  output [31:0] VEC_LANE3,
  output IS_VECTOR
);

  wire dmem_we;
  wire [31:0] dmem_addr, dmem_rdata, dmem_wdata, imem_addr, imem_data;

  riscv_cpu_vector #(.applicationType("GHDL"), .ghdlOptions("--std=08 --ieee=synopsys"), .CodeFile("riscv_cpu_vector.vhd")) u_riscv_cpu_vector (
    .clk_i(CLOCK), .reset_i(RESET), .load_enable_i(LOAD_ENABLE), .imem_data_i(imem_data),
    .dmem_rdata_i(dmem_rdata), .reg_sel_i(REG_SEL), .imem_addr_o(imem_addr), .dmem_addr_o(dmem_addr),
    .dmem_wdata_o(dmem_wdata), .dmem_we_o(dmem_we), .pc_debug_o(PC), .instr_debug_o(INSTR),
    .alu_result_debug_o(ALU_RESULT), .reg_debug_o(REG_DEBUG), .hazard_stall_o(HAZARD_STALL),
    .hazard_flush_o(HAZARD_FLUSH), .vec_lane0_debug_o(VEC_LANE0), .vec_lane1_debug_o(VEC_LANE1),
    .vec_lane2_debug_o(VEC_LANE2), .vec_lane3_debug_o(VEC_LANE3), .is_vector_debug_o(IS_VECTOR));
  ROM #(.AddrBits(8), .Bits(32)) ROM_INSTR (.A(imem_addr[9:2]), .sel(LOAD_ENABLE), .D(imem_data));
  RAMDualPort #(.AddrBits(8), .Bits(32)) RAM_DADOS (
    .A(dmem_addr[9:2]), .Din(dmem_wdata), .str(dmem_we), .C(CLOCK), .ld(LOAD_ENABLE), .D(dmem_rdata));

  // Other names for the same wires on the sheet: alu_debug[31:0] = ALU_RESULT; clk = CLOCK;
  //   ram_addr[7:0] = dmem_addr[9:2]; hz_flush = HAZARD_FLUSH; hz_stall = HAZARD_STALL;
  //   rom_addr[7:0] = imem_addr[9:2]; instr_debug[31:0] = INSTR; is_vec = IS_VECTOR; load_en = LOAD_ENABLE;
  //   pc_debug[31:0] = PC; vlane0[31:0] = VEC_LANE0; vlane1[31:0] = VEC_LANE1; vlane2[31:0] = VEC_LANE2;
  //   vlane3[31:0] = VEC_LANE3

  // Notes on the sheet:
  //   contents of ROM_INSTR (hex, n*v repeats v):
  //   50008b,30010b,2081db,4020825b,20928b,10d30b,2093db,6f
endmodule
